// Logisim project 332_Project_10_Bit_CPU.circ as structural Verilog: 4 circuits, main circuit main
module main (
  input  in_1,
  output Zero_flag,
  output [3:0] op,
  output [1:0] RD,
  output [1:0] RS,
  output [1:0] RT,
  output [1:0] Imm,
  output [9:0] A,
  output [9:0] Alu_result,
  output [9:0] mem_or_alu_result,
  output [9:0] B
);

  wire and_1_out, Clock_out, control_1_beq_label, control_1_bew_control, control_1_bne, control_1_lw,
       control_1_mem_enb, control_1_mem_reg, control_1_reg_imm, control_1_reg_write, control_1_sw,
       multiplexer_4_out, xor_1_out;
  wire [9:0] adder_1_out, adder_2_out, bit_extender_1_out, multiplexer_1_out, multiplexer_3_out, PC_q,
       ram_1_data, register_file_10_bits_1_data02, shifter_1_out;

  Clock Clock (.out(Clock_out));
  Register #(.width(10)) PC (.D(multiplexer_3_out), .Q(PC_q), .clk(Clock_out));  // open: en, clr
  Adder #(.width(10)) adder_1 (.a(PC_q), .b(10'h1), .out(adder_1_out));  // open: cin, cout
  control control_1 (
    .Opcode(op), .reg_write(control_1_reg_write), .reg_imm(control_1_reg_imm),
    .beq_label(control_1_beq_label), .bew_control(control_1_bew_control), .mem_enb(control_1_mem_enb),
    .lw(control_1_lw), .sw(control_1_sw), .mem_reg(control_1_mem_reg), .bne(control_1_bne));
  ROM #(.addrWidth(10), .dataWidth(10)) rom_1 (.addr(PC_q), .data({op, RD, RS, Imm}));  // open: sel
  assign bit_extender_1_out = {{8{1'b0}}, Imm};  // Bit_Extender bit_extender_1
  Register_file_10_bits register_file_10_bits_1 (
    .Data_IN(mem_or_alu_result), .Reg_Write(control_1_reg_write), .Clock(Clock_out), .Data01(A),
    .Data02(register_file_10_bits_1_data02), .RD_Data_Address(RD), .RS(RS), .RT(Imm));
  Shifter #(.width(10)) shifter_1 (.in(bit_extender_1_out), .\dist (4'b0000), .out(shifter_1_out));
  Multiplexer #(.width(10), .enable("false")) multiplexer_1 (
    .in0(bit_extender_1_out), .in1(register_file_10_bits_1_data02), .out(multiplexer_1_out),
    .sel(control_1_beq_label));
  Multiplexer #(.width(10), .enable("false")) multiplexer_2 (
    .in0(register_file_10_bits_1_data02), .in1(multiplexer_1_out), .out(B), .sel(control_1_reg_imm));
  Adder #(.width(10)) adder_2 (.a(adder_1_out), .b(shifter_1_out), .out(adder_2_out));  // open: cin, cout
  ALU_10bits alu_10bits_1 (.Result(Alu_result), .Operand_B(B), .Operand_A(A), .Alu_Opcode(op), .ZeroFlag(Zero_flag));
  Multiplexer #(.width(10), .enable("false")) multiplexer_3 (
    .in0(adder_1_out), .in1(adder_2_out), .out(multiplexer_3_out), .sel(multiplexer_4_out));
  and and_1 (and_1_out, control_1_bew_control, Zero_flag);
  Multiplexer #(.enable("false")) multiplexer_4 (
    .in0(and_1_out), .in1(xor_1_out), .out(multiplexer_4_out), .sel(control_1_bne));
  xor xor_1 (xor_1_out, control_1_bne, Zero_flag);
  RAM #(.addrWidth(10), .dataWidth(10), .bus("separate")) ram_1 (
    .addr(Alu_result), .din(register_file_10_bits_1_data02), .data(ram_1_data), .str(control_1_sw),
    .sel(control_1_mem_enb), .clk(Clock_out), .ld(control_1_lw), .clr(in_1));
  Multiplexer #(.width(10), .enable("false")) multiplexer_5 (
    .in0(Alu_result), .in1(ram_1_data), .out(mem_or_alu_result), .sel(control_1_mem_reg));

  assign RT = Imm;

  // Notes on the sheet:
  //   instruction Memory
  //   contents of rom_1 (hex, n*v repeats v):
  //   86 c6
  //   beq
  //   bne
  //   Data Memory
endmodule

module ALU_10bits (
  input  [9:0] Operand_B,
  input  [9:0] Operand_A,
  input  [3:0] Alu_Opcode,
  output ZeroFlag,
  output [9:0] Result
);

  wire [9:0] adder_1_out, adder_2_out, and_1_out, not_1_out, or_1_out;

  assign not_1_out = ~Operand_B;  // NOT_Gate not_1, 10 bits wide
  Adder #(.width(10)) adder_1 (.a(Operand_B), .b(Operand_A), .out(adder_1_out));  // open: cin, cout
  Adder #(.width(10)) adder_2 (.a(Operand_A), .b(not_1_out), .out(adder_2_out), .cin(1'b1));  // open: cout
  assign and_1_out = Operand_A & Operand_B;  // AND_Gate and_1, 10 bits wide
  assign or_1_out = Operand_A | Operand_B;  // OR_Gate or_1, 10 bits wide
  Multiplexer #(.select(4), .width(10), .enable("false")) multiplexer_1 (
    .in0(adder_1_out), .in1(adder_2_out), .in2(adder_1_out), .in3(adder_1_out), .in4(and_1_out),
    .in5(and_1_out), .in6(or_1_out), .in7(or_1_out), .in8(adder_2_out), .in9(adder_2_out), .out(Result),
    .sel(Alu_Opcode));  // open: in10, in11, in12, in13, in14, in15
  nor nor_1 (ZeroFlag, Result[0], Result[1], Result[2], Result[3], Result[4], Result[5], Result[6], Result[7], Result[8], Result[9]);
endmodule

module Register_file_10_bits (
  input  [9:0] Data_IN,
  input  Reg_Write,
  input  [1:0] RD_Data_Address,
  input  [1:0] RS,
  input  Clock,
  input  [1:0] RT,
  output [9:0] Data01,
  output [9:0] Data02
);

  wire and_1_out, and_2_out, and_3_out, and_4_out, decoder_1_out0, decoder_1_out1, decoder_1_out2,
       decoder_1_out3;
  wire [9:0] R0_q, R1_q, R2_q, R3_q;

  Decoder #(.select(2)) decoder_1 (
    .out0(decoder_1_out0), .out1(decoder_1_out1), .out2(decoder_1_out2), .out3(decoder_1_out3),
    .sel(RD_Data_Address));  // open: en
  and and_1 (and_1_out, Reg_Write, decoder_1_out0);
  and and_2 (and_2_out, Reg_Write, decoder_1_out1);
  and and_3 (and_3_out, Reg_Write, decoder_1_out2);
  and and_4 (and_4_out, Reg_Write, decoder_1_out3);
  Register #(.width(10)) R0 (.D(Data_IN), .en(and_1_out), .Q(R0_q), .clk(Clock));  // open: clr
  Register #(.width(10)) R1 (.D(Data_IN), .en(and_2_out), .Q(R1_q), .clk(Clock));  // open: clr
  Register #(.width(10)) R2 (.D(Data_IN), .en(and_3_out), .Q(R2_q), .clk(Clock));  // open: clr
  Register #(.width(10)) R3 (.D(Data_IN), .en(and_4_out), .Q(R3_q), .clk(Clock));  // open: clr
  Multiplexer #(.select(2), .width(10)) multiplexer_1 (
    .in0(R0_q), .in1(R1_q), .in2(R2_q), .in3(R3_q), .out(Data01), .sel(RS));  // open: en
  Multiplexer #(.select(2), .width(10)) multiplexer_2 (
    .in0(R0_q), .in1(R1_q), .in2(R2_q), .in3(R3_q), .out(Data02), .sel(RT));  // open: en
endmodule

module control (
  input  [3:0] Opcode,
  output reg_write,
  output reg_imm,
  output beq_label,
  output bew_control,
  output mem_enb,
  output lw,
  output sw,
  output mem_reg,
  output bne
);

  wire and_2_out, and_3_out, not_2_out, not_3_out, not_4_out, not_5_out, not_6_out, not_7_out;

  not not_1 (reg_write, Opcode[3]);
  not not_2 (not_2_out, Opcode[2]);
  not not_3 (not_3_out, Opcode[2]);
  not not_4 (not_4_out, Opcode[2]);
  not not_5 (not_5_out, Opcode[0]);
  not not_6 (not_6_out, Opcode[2]);
  not not_7 (not_7_out, Opcode[2]);
  and and_1 (bne, Opcode[3], Opcode[0]);
  and and_2 (and_2_out, not_2_out, Opcode[1]);
  and and_3 (and_3_out, Opcode[2], Opcode[0]);
  and and_4 (mem_enb, not_3_out, Opcode[1]);
  and and_5 (lw, not_4_out, Opcode[1], not_5_out);
  and and_6 (sw, not_6_out, Opcode[1], Opcode[0]);
  and and_7 (mem_reg, not_7_out, Opcode[1]);
  or or_1 (reg_imm, and_2_out, and_3_out, Opcode[3]);

  assign beq_label = Opcode[3];
  assign bew_control = Opcode[3];
endmodule
